# Fritzing sketch BoomBalloon-Wiring (saved by Fritzing 0.9.6b)

parts:
  J1 = Fotomodul [package=THT]
  J2 = Displaymodul [package=THT]
  J3 = Steuermodul [package=THT]
  J4 = Lichtmodul [package=THT]
  PUMP = DC Motor
  POWER = Power Jack [package=power_jack_pth]
  S1 = Taiway 100-SP-X-T1 SPDT Miniature Toggle Switch [part_number=100-SP-X-T1-0-0-B1-M1 package=THT]
  VALVE = DC Motor

nets:
  N1: J1.3V3, J3.FM_3V3
  N2: J1.GND#1, J3.FM_GND
  N3: J1.A0, J3.FM_A0
  N4: J1.A1, J3.FM_A1
  N5: J1.A2, J3.FM_A2
  N6: J1.A3, J3.FM_A3
  N7: J1.A4, J3.FM_A4
  N8: J1.LM1, J4.LM1
  N9: J1.LM2, J4.LM2
  VCC: J1.Vcc, J2.Vcc, J3.DM_Vcc
  N10: J1.GND#10, J2.GND, J3.DM_GND
  N11: J1.DS, J2.DS, J3.DM_DS
  N12: J1.STCP, J2.STCP, J3.DM_STCP
  N13: J1.SHCP, J2.SHCP, J3.DM_SHCP
  N14: J1.Buzzer, J2.Buzzer, J3.DM_Buzzer
  N15: J3.VA, VALVE.pin_1
  N16: J3.MA, VALVE.pin_2
  N17: J3.VM, PUMP.pin_1
  N18: J3.MM, PUMP.pin_2
  N19: J3.+12V, S1.L2
  N20: J3.GND_12V, POWER.GND
  N21: POWER.PWR, S1.COM

custom parts:
  Fotomodul: Fotomodul -- BoomBalloon custom Fritzing part, generated from the real PCB Gerbers.
  Displaymodul: Displaymodul -- BoomBalloon custom Fritzing part, generated from the real PCB Gerbers.
  Steuermodul: Steuermodul -- BoomBalloon custom Fritzing part, generated from the real PCB Gerbers.
  Lichtmodul: Lichtmodul -- BoomBalloon custom Fritzing part, generated from the real PCB Gerbers.
